# Fritzing sketch random_notes_with_speed_and_velocity_control (saved by Fritzing 0.9.3b)
breadboards: 1

parts:
  Part1 = Arduino Uno (Rev3)
  LED1 = smd LED [color="Red (633nm)" package="1206 [SMD]"]
  S1 = Pushbutton Streteched to 300x200mil [package="[THT]"]
  R2 = Trimmer Potentiometer [maximum_resistance=10kΩ package=THT]
  R3 = Photocell (LDR) [package=THT]
  R1 = Resistor [tolerance=±5% resistance=220 package="2512 [SMD]"]
  R4 = Resistor [tolerance=±5% resistance=220 package=THT]

nets:
  N1: Part1.A0, R2.wiper
  N2: Part1.A1, R3.pin_0, R4.Pin_1
  N3: Part1.D13/SCK, R1.Pin_1
  N4: Part1.GND, S1.Pin_3, S1.Pin_4, R2.leg2, R4.Pin_0
  N5: Part1.D2, S1.Pin_1, S1.Pin_2
  N6: LED1.anode, R1.Pin_0
  N7: R2.leg1, R3.pin_1

notes:
  220 ohm
  10k ohm

custom parts:
  Pushbutton Streteched to 300x200mil: A generic pushbutton stretched to fit a 100mil grid.
